// Digital circuit Chave-lógica.dig as structural Verilog
module \Chave_lógica  (
  input  E,
  input  S0,
  input  S1,
  output SD
);

  wire and_1_out, and_2_out, not_1_out;

  not not_1 (not_1_out, E);
  and and_1 (and_1_out, E, S0);
  and and_2 (and_2_out, not_1_out, S1);
  or or_1 (SD, and_1_out, and_2_out);
endmodule
