// Digital circuit Contador.dig as structural Verilog
module Contador (
  input  CLK,
  input  E1,
  input  EN,
  output S1,
  output S2,
  output S3,
  output S4
);

  wire flip_flop_jk_presclr_1_nq, flip_flop_jk_presclr_2_nq, flip_flop_jk_presclr_3_nq,
       flip_flop_jk_presclr_4_nq;

  Flip_Flop_JK_PresClr flip_flop_jk_presclr_1 (
    .J(E1), .K(E1), .CLK(CLK), .Preset(EN), .Clr(E1), .Q(S1), .nQ(flip_flop_jk_presclr_1_nq));
  LED led_1 (.in(flip_flop_jk_presclr_1_nq));
  Flip_Flop_JK_PresClr flip_flop_jk_presclr_2 (
    .J(E1), .K(E1), .CLK(S1), .Preset(EN), .Clr(E1), .Q(S2), .nQ(flip_flop_jk_presclr_2_nq));
  LED led_2 (.in(flip_flop_jk_presclr_2_nq));
  Flip_Flop_JK_PresClr flip_flop_jk_presclr_3 (
    .J(E1), .K(E1), .CLK(S2), .Preset(EN), .Clr(E1), .Q(S3), .nQ(flip_flop_jk_presclr_3_nq));
  LED led_3 (.in(flip_flop_jk_presclr_3_nq));
  Flip_Flop_JK_PresClr flip_flop_jk_presclr_4 (
    .J(E1), .K(E1), .CLK(S3), .Preset(EN), .Clr(E1), .Q(S4), .nQ(flip_flop_jk_presclr_4_nq));
  LED led_4 (.in(flip_flop_jk_presclr_4_nq));
endmodule
