// Digital circuit Célula Memória.dig as structural Verilog
module \Célula_Memória  (
  input  CLK,
  input  E1,
  input  E2,
  input  EN,
  input  CLEAR,
  input  E3,
  input  E4,
  input  E5,
  input  E6,
  input  E7,
  input  E8,
  output S1,
  output S2,
  output S3,
  output S4,
  output S5,
  output S6,
  output S7,
  output S8
);

  wire flip_flop_d_1_o, flip_flop_d_2_o, flip_flop_d_3_o, flip_flop_d_4_o, flip_flop_d_5_o, flip_flop_d_6_o,
       flip_flop_d_7_o, flip_flop_d_8_o, not_1_out;

  not not_1 (not_1_out, CLEAR);
  flip_flop_D flip_flop_d_1 (.CL(CLK), .D(E1), .EN(EN), .O(flip_flop_d_1_o));  // open: O_2
  and and_1 (S1, flip_flop_d_1_o, not_1_out);
  flip_flop_D flip_flop_d_2 (.CL(CLK), .D(E2), .EN(EN), .O(flip_flop_d_2_o));  // open: O_2
  flip_flop_D flip_flop_d_3 (.CL(CLK), .D(E3), .EN(EN), .O(flip_flop_d_3_o));  // open: O_2
  and and_2 (S2, flip_flop_d_2_o, not_1_out);
  flip_flop_D flip_flop_d_4 (.CL(CLK), .D(E4), .EN(EN), .O(flip_flop_d_4_o));  // open: O_2
  and and_3 (S3, flip_flop_d_3_o, not_1_out);
  flip_flop_D flip_flop_d_5 (.CL(CLK), .D(E5), .EN(EN), .O(flip_flop_d_5_o));  // open: O_2
  and and_4 (S4, flip_flop_d_4_o, not_1_out);
  flip_flop_D flip_flop_d_6 (.CL(CLK), .D(E6), .EN(EN), .O(flip_flop_d_6_o));  // open: O_2
  and and_5 (S5, flip_flop_d_5_o, not_1_out);
  and and_6 (S6, flip_flop_d_6_o, not_1_out);
  flip_flop_D flip_flop_d_7 (.CL(CLK), .D(E7), .EN(EN), .O(flip_flop_d_7_o));  // open: O_2
  and and_7 (S7, flip_flop_d_7_o, not_1_out);
  flip_flop_D flip_flop_d_8 (.CL(CLK), .D(E8), .EN(EN), .O(flip_flop_d_8_o));  // open: O_2
  and and_8 (S8, flip_flop_d_8_o, not_1_out);
endmodule
