// Digital circuit Decodificador.dig as structural Verilog
module Decodificador (
  input  in_1,
  input  in_2,
  input  in_3,
  input  in_4,
  output out_5,
  output out_6,
  output out_7,
  output out_8,
  output out_9
);

  wire and_1_out, and_2_out, and_3_out, and_4_out, and_5_out, not_1_out, not_2_out, not_3_out, not_4_out;

  not not_1 (not_1_out, in_1);
  not not_2 (not_2_out, in_2);
  not not_3 (not_3_out, in_3);
  not not_4 (not_4_out, in_4);
  and and_1 (and_1_out, not_1_out, not_2_out, not_3_out, not_4_out);
  and and_2 (and_2_out, not_1_out, not_2_out, not_3_out, in_4);
  and and_3 (and_3_out, not_1_out, not_2_out, in_3, not_4_out);
  and and_4 (and_4_out, not_1_out, not_2_out, in_3, in_4);
  and and_5 (and_5_out, not_1_out, in_2, not_3_out, not_4_out);
  not not_5 (out_5, and_1_out);
  not not_6 (out_6, and_2_out);
  not not_7 (out_7, and_3_out);
  not not_8 (out_8, and_4_out);
  not not_9 (out_9, and_5_out);
endmodule
