// Digital circuit Flip-Flop-EscravoMestre.dig as structural Verilog
module Flip_Flop_EscravoMestre (
  input  J,
  input  CLK,
  input  K,
  input  Preset,
  input  Clr,
  input  EN,
  output O,
  output O_2
);

  wire nand_1_out, nand_2_out, nand_3_out, nand_4_out, nand_5_out, nand_6_out, not_1_out;

  nand nand_1 (nand_1_out, CLK, CLK, O, EN);
  nand nand_2 (nand_2_out, K, CLK, O_2, EN);
  not not_1 (not_1_out, CLK);
  nand nand_3 (nand_3_out, nand_2_out, Clr, nand_4_out);
  nand nand_4 (nand_4_out, nand_1_out, Preset, nand_3_out);
  nand nand_5 (nand_5_out, nand_3_out, not_1_out);
  nand nand_6 (nand_6_out, nand_4_out, not_1_out);
  nand nand_7 (O, nand_5_out, O_2);
  nand nand_8 (O_2, nand_6_out, Preset, O);

  assign J = CLK;
endmodule
