// Digital circuit Flip-Flop-JK-PresClr.dig as structural Verilog
module Flip_Flop_JK_PresClr (
  input  J,
  input  K,
  input  CLK,
  input  Preset,
  input  Clr,
  output Q,
  output nQ
);

  wire nand_1_out, nand_2_out, nand_3_out, nand_4_out, nand_5_out, nand_6_out, not_1_out;

  nand nand_1 (nand_1_out, J, CLK, nQ);
  nand nand_2 (nand_2_out, K, CLK, Q);
  not not_1 (not_1_out, CLK);
  nand nand_3 (nand_3_out, nand_1_out, Preset, nand_4_out);
  nand nand_4 (nand_4_out, nand_2_out, Clr, nand_3_out);
  nand nand_5 (nand_5_out, nand_3_out, not_1_out);
  nand nand_6 (nand_6_out, nand_4_out, not_1_out);
  nand nand_7 (Q, nand_5_out, Preset, nQ);
  nand nand_8 (nQ, nand_6_out, Clr, Q);
endmodule
