// Digital circuit Flip-Flop-JK.dig as structural Verilog
module Flip_Flop_JK (
  input  J,
  input  K,
  input  Clk,
  input  EN,
  output O,
  output O_2
);

  wire and_1_out, and_2_out;

  and and_1 (and_1_out, O, EN, J, Clk);
  and and_2 (and_2_out, Clk, K, EN, O_2);
  // NOr nor_1 has open pins: In_1=and_1_out, In_2=O_2, out=open
  // NOr nor_2 has open pins: In_1=O, In_2=and_2_out, out=open
endmodule
