// Digital circuit Meio-Somador.dig as structural Verilog
module Meio_Somador (
  input  E1,
  input  E2,
  output SUM,
  output CARRY
);

  and and_1 (CARRY, E2, E1);
  xor xor_1 (SUM, E2, E1);
endmodule
