// Digital circuit Memória RAM.dig as structural Verilog
module \Memória_RAM  (
  input  clk,
  input  in_2
);

  \Célula_Memória  \célula_memória_1  (.clk(clk));
  \Célula_Memória  \célula_memória_2  (.clk(clk));
  \Célula_Memória  \célula_memória_3  (.clk(clk));
  \Célula_Memória  \célula_memória_4  (.clk(clk));
  \Célula_Memória  \célula_memória_5  (.clk(clk));
  \Célula_Memória  \célula_memória_6  (.clk(clk));
  \Célula_Memória  \célula_memória_7  (.clk(clk));
  \Célula_Memória  \célula_memória_8  (.clk(clk));
  \Célula_Memória  \célula_memória_9  (.clk(clk));
  \Célula_Memória  \célula_memória_10  (.clk(clk));
  \Célula_Memória  \célula_memória_11  (.clk(clk));
  \Célula_Memória  \célula_memória_12  (.clk(clk));
  \Célula_Memória  \célula_memória_13  (.clk(clk));
  \Célula_Memória  \célula_memória_14  (.clk(clk));
  \Célula_Memória  \célula_memória_15  (.clk(clk));
  \Célula_Memória  \célula_memória_16  (.clk(clk));
endmodule
