// Digital circuit Reg8Bts.dig as structural Verilog
module Reg8Bts (
  input  E1,
  input  E2,
  input  E3,
  input  E4,
  input  E5,
  input  E6,
  input  E7,
  input  E8,
  input  Clk,
  input  EN,
  output S1,
  output S2,
  output S3,
  output S4,
  output S5,
  output S6,
  output S7,
  output S8
);

  wire not_1_out;

  not not_1 (not_1_out, EN);
  flip_flop_D flip_flop_d_1 (.CL(Clk), .D(E1), .En(not_1_out));
  flip_flop_D flip_flop_d_2 (.CL(Clk), .D(E2), .En(not_1_out));
  flip_flop_D flip_flop_d_3 (.CL(Clk), .D(E3), .En(not_1_out));
  flip_flop_D flip_flop_d_4 (.CL(Clk), .D(E4), .En(not_1_out));
  flip_flop_D flip_flop_d_5 (.CL(Clk), .D(E5), .En(not_1_out));
  flip_flop_D flip_flop_d_6 (.CL(Clk), .D(E6), .En(not_1_out));
  flip_flop_D flip_flop_d_7 (.CL(Clk), .D(E7), .En(not_1_out));
  flip_flop_D flip_flop_d_8 (.CL(Clk), .D(E8), .En(not_1_out));
endmodule
