// Digital circuit Registrador-Ende.dig as structural Verilog
module Registrador_Ende (
  input  EN,
  input  CLK,
  input  E1,
  input  E2,
  input  E3,
  input  E4,
  output S1,
  output S2,
  output S3,
  output S4
);

  flip_flop_D flip_flop_d_1 (.CL(CLK), .D(E1), .EN(EN), .O(S1));  // open: O_2
  flip_flop_D flip_flop_d_2 (.CL(CLK), .D(E2), .EN(EN), .O(S2));  // open: O_2
  flip_flop_D flip_flop_d_3 (.CL(CLK), .D(E3), .EN(EN), .O(S3));  // open: O_2
  flip_flop_D flip_flop_d_4 (.CL(CLK), .D(E4), .EN(EN), .O(S4));  // open: O_2
endmodule
