// Digital circuit RegistradorD4Bts.dig as structural Verilog
module RegistradorD4Bts (
  input  E1,
  input  E2,
  input  E3,
  input  E4,
  output S1,
  output S2,
  output S3,
  output S4,
  output S5,
  output S6,
  output S7,
  output S8,
  output S9,
  output S10,
  output S11,
  output S12,
  output S13,
  output S14,
  output S15
);

  wire not_1_out, not_2_out, not_3_out, not_4_out, not_5_out, not_6_out, not_7_out, not_8_out, not_9_out,
       not_10_out, not_11_out, not_12_out, not_13_out, not_14_out, not_15_out, not_16_out, not_17_out,
       not_18_out, not_19_out, not_20_out, not_21_out, not_22_out, not_23_out, not_24_out, not_25_out,
       not_26_out, not_27_out, not_28_out;

  not not_1 (not_1_out, E4);
  not not_2 (not_2_out, E4);
  not not_3 (not_3_out, E4);
  not not_4 (not_4_out, E4);
  not not_5 (not_5_out, E4);
  not not_6 (not_6_out, E4);
  not not_7 (not_7_out, E4);
  not not_8 (not_8_out, E3);
  not not_9 (not_9_out, E3);
  not not_10 (not_10_out, E3);
  not not_11 (not_11_out, E3);
  not not_12 (not_12_out, E3);
  not not_13 (not_13_out, E3);
  not not_14 (not_14_out, E3);
  not not_15 (not_15_out, E2);
  not not_16 (not_16_out, E2);
  not not_17 (not_17_out, E2);
  not not_18 (not_18_out, E2);
  not not_19 (not_19_out, E2);
  not not_20 (not_20_out, E2);
  not not_21 (not_21_out, E2);
  not not_22 (not_22_out, E1);
  not not_23 (not_23_out, E1);
  not not_24 (not_24_out, E1);
  not not_25 (not_25_out, E1);
  not not_26 (not_26_out, E1);
  not not_27 (not_27_out, E1);
  not not_28 (not_28_out, E1);
  and and_1 (S1, E1, not_15_out, not_8_out, not_1_out);
  and and_2 (S2, not_24_out, E2, not_9_out, not_2_out);
  and and_3 (S3, E1, E2, not_10_out, not_3_out);
  and and_4 (S4, not_25_out, not_16_out, E3, not_4_out);
  and and_5 (S5, E1, not_17_out, E3, not_5_out);
  and and_6 (S6, not_26_out, E2, E3, not_6_out);
  and and_7 (S7, E1, E2, E3, not_7_out);
  and and_8 (S8, not_27_out, not_18_out, not_11_out, E4);
  and and_9 (S9, E1, not_19_out, not_12_out, E4);
  and and_10 (S10, not_28_out, E2, not_13_out, E4);
  and and_11 (S11, E1, E2, not_14_out, E4);
  and and_12 (S12, not_22_out, not_20_out, E3, E4);
  and and_13 (S13, E1, not_21_out, E3, E4);
  and and_14 (S14, not_23_out, E2, E3, E4);
  and and_15 (S15, E1, E2, E3, E4);
endmodule
