// Digital circuit SAP-1.dig as structural Verilog
module SAP_1 (
  input  in_1,
  input  clk,
  input  in_3,
  input  in_4,
  input  in_5
);

  wire [3:0] counter_1_out;

  Counter #(.Bits(4)) counter_1 (.en(in_1), .C(clk), .clr(in_3), .out(counter_1_out));  // open: ovf
  Register register_1 (.D(counter_1_out[0]));  // open: C, en, Q
  Register register_2 (.C(clk));  // open: D, en, Q
  Register register_3 (.D(in_4), .C(clk), .en(in_5));  // open: Q
  // Pins of 1 and 4 bits meet at counter_1_out
endmodule
