// Digital circuit Somador-Completo.dig as structural Verilog
module Somador_Completo (
  input  E1,
  input  E2,
  input  Cin,
  output SUM,
  output CARRY
);

  wire and_1_out, and_2_out, and_3_out;

  or or_1 (CARRY, and_3_out, and_2_out, and_1_out);
  and and_1 (and_1_out, E2, E1);
  and and_2 (and_2_out, Cin, E1);
  and and_3 (and_3_out, Cin, E2);
  xor xor_1 (SUM, Cin, E2, E1);
endmodule
