// Digital circuit ULA.dig as structural Verilog
module ULA (
  input  CIN,
  input  S0,
  input  S1,
  input  EN1,
  input  EN2,
  input  EN3,
  input  EN4,
  input  EN5,
  input  EN6,
  input  EN7,
  input  EN8,
  input  E1,
  input  E2,
  input  E3,
  input  E4,
  input  E5,
  input  E6,
  input  E7,
  input  E8,
  output S1_2,
  output S2,
  output S3,
  output S4,
  output S5,
  output S6,
  output S7,
  output S8
);

  wire \chave_lógica_1_sd , \chave_lógica_2_sd , \chave_lógica_3_sd , \chave_lógica_4_sd ,
       \chave_lógica_5_sd , \chave_lógica_6_sd , \chave_lógica_7_sd , \chave_lógica_8_sd ,
       somador_completo_1_carry, somador_completo_2_p1, somador_completo_2_p5, somador_completo_3_carry,
       somador_completo_4_carry, somador_completo_5_carry, somador_completo_6_carry, somador_completo_7_carry;

  \Chave_lógica  \chave_lógica_1  (.E(E1), .S0(S0), .S1(S1), .SD(\chave_lógica_1_sd ));
  \Chave_lógica  \chave_lógica_2  (.E(E2), .S0(S0), .S1(S1), .SD(\chave_lógica_2_sd ));
  \Chave_lógica  \chave_lógica_3  (.E(E3), .S0(S0), .S1(S1), .SD(\chave_lógica_3_sd ));
  \Chave_lógica  \chave_lógica_4  (.E(E4), .S0(S0), .S1(S1), .SD(\chave_lógica_4_sd ));
  \Chave_lógica  \chave_lógica_5  (.E(E5), .S0(S0), .S1(S1), .SD(\chave_lógica_5_sd ));
  \Chave_lógica  \chave_lógica_6  (.E(E6), .S0(S0), .S1(S1), .SD(\chave_lógica_6_sd ));
  \Chave_lógica  \chave_lógica_7  (.E(E7), .S0(S0), .S1(S1), .SD(\chave_lógica_7_sd ));
  \Chave_lógica  \chave_lógica_8  (.E(E8), .S0(S0), .S1(S1), .SD(\chave_lógica_8_sd ));
  Somador_Completo somador_completo_1 (
    .E1(EN1), .E2(\chave_lógica_1_sd ), .Cin(CIN), .SUM(S1_2), .CARRY(somador_completo_1_carry));
  // Somador_Completo somador_completo_2: pin names not known; wires that end beside it: somador_completo_2_p1, \chave_lógica_2_sd , somador_completo_1_carry, S2, somador_completo_2_p5
  Somador_Completo somador_completo_3 (
    .E1(EN3), .E2(\chave_lógica_3_sd ), .Cin(somador_completo_2_p5), .SUM(S3),
    .CARRY(somador_completo_3_carry));
  Somador_Completo somador_completo_4 (
    .E1(EN4), .E2(\chave_lógica_4_sd ), .Cin(somador_completo_3_carry), .SUM(S4),
    .CARRY(somador_completo_4_carry));
  Somador_Completo somador_completo_5 (
    .E1(EN5), .E2(\chave_lógica_5_sd ), .Cin(somador_completo_4_carry), .SUM(S5),
    .CARRY(somador_completo_5_carry));
  Somador_Completo somador_completo_6 (
    .E1(EN6), .E2(\chave_lógica_6_sd ), .Cin(somador_completo_5_carry), .SUM(S6),
    .CARRY(somador_completo_6_carry));
  Somador_Completo somador_completo_7 (
    .E1(EN7), .E2(\chave_lógica_7_sd ), .Cin(somador_completo_6_carry), .SUM(S7),
    .CARRY(somador_completo_7_carry));
  Somador_Completo somador_completo_8 (
    .E1(EN8), .E2(\chave_lógica_8_sd ), .Cin(somador_completo_7_carry), .SUM(S8));  // open: CARRY
endmodule
