// Digital circuit flip-flop-D.dig as structural Verilog
module flip_flop_D (
  input  D,
  input  in_2
);

  wire nand_1_out, nand_2_out, nor_1_out, nor_2_out, not_1_out;

  not not_1 (not_1_out, in_2);
  nand nand_1 (nand_1_out, in_2, D);
  nand nand_2 (nand_2_out, D, not_1_out);
  nor nor_1 (nor_1_out, nor_2_out, nand_1_out);
  nor nor_2 (nor_2_out, nand_2_out, nor_1_out);
  LED led_1 (.in(nor_1_out));
  LED led_2 (.in(nor_2_out));
endmodule
